# Fritzing sketch Esquema (saved by Fritzing 0.9.3b)
breadboards: 1

parts:
  LED1 = LED - 5mm [color="Red (633nm)" package="5 mm [THT]"]
  R1 = Resistor [tolerance=±5% resistance=220 package=THT]
  R2 = Resistor [tolerance=±5% resistance=220 package=THT]
  LED2 = LED - 5mm [color="Red (633nm)" package="5 mm [THT]"]
  R3 = Photocell (LDR) [package=THT]
  R4 = Resistor [tolerance=±5% resistance=220 package=THT]
  Componente1 = Arduino Uno (Rev3)  # not connected
  Componente2 = Arduino Wireless SD Shield
  J1 = Infrared Proximity Sensor
  U1 = XBee  # not connected

nets:
  N1: LED1.cathode, R1.Pin_1
  N2: LED1.anode, Componente2.D2
  GND: R1.Pin_0, R2.Pin_0, R4.Pin_0, Componente2.GND, J1.GND
  N3: R2.Pin_1, LED2.cathode
  N4: LED2.anode, Componente2.D3
  N5: R3.pin_0, R4.Pin_1, Componente2.A0
  +5V: R3.pin_1, Componente2.+5V, J1.Vcc
  N6: Componente2.SD_CS, J1.Vout
